// Logisim project CHESS  BOARD CHIP.circ as structural Verilog: 5 circuits, main circuit MAIN CIRCUIT CHIP
// Steps counter
module STEPS_CALCULATOR (
  input  [1:0] S,
  input  [2:0] Xf,
  input  [2:0] Yf,
  input  Xf_Xi,
  input  Xf_Xi_2,
  input  Xf_Xi_3,
  input  Yf_Yi,
  input  Yf_Yi_2,
  input  Yf_Yi_3,
  input  [2:0] Xi,
  input  [2:0] Yi,
  output [2:0] STEPS
);

  wire comparator_1_eq, xor_1_out;
  wire [2:0] multiplexer_1_out, multiplexer_2_out, multiplexer_3_out, multiplexer_4_out, multiplexer_5_out,
       multiplexer_6_out, subtractor_1_out, subtractor_2_out;

  Multiplexer #(.width(3), .enable("false")) multiplexer_1 (.in0(Xi), .in1(Xf), .out(multiplexer_1_out), .sel(Xf_Xi));
  Multiplexer #(.width(3), .enable("false")) multiplexer_2 (.in0(Xi), .in1(Xf), .out(multiplexer_2_out), .sel(Xf_Xi_3));
  Multiplexer #(.width(3), .enable("false")) multiplexer_3 (.in0(Yi), .in1(Yf), .out(multiplexer_3_out), .sel(Yf_Yi));
  Multiplexer #(.width(3), .enable("false")) multiplexer_4 (.in0(Yi), .in1(Yf), .out(multiplexer_4_out), .sel(Yf_Yi_3));
  Subtractor #(.width(3)) subtractor_1 (
    .a(multiplexer_1_out), .b(multiplexer_2_out), .out(subtractor_1_out));  // open: bin, bout
  Subtractor #(.width(3)) subtractor_2 (
    .a(multiplexer_3_out), .b(multiplexer_4_out), .out(subtractor_2_out));  // open: bin, bout
  Comparator #(.width(3), .mode("unsigned")) comparator_1 (
    .a(subtractor_1_out), .b(subtractor_2_out), .eq(comparator_1_eq));  // open: gt, lt
  Multiplexer #(.width(3), .enable("false")) multiplexer_5 (
    .in0(3'b000), .in1(subtractor_1_out), .out(multiplexer_5_out), .sel(comparator_1_eq));
  xor xor_1 (xor_1_out, S[0], S[1]);
  Multiplexer #(.width(3), .enable("false")) multiplexer_6 (
    .in0(multiplexer_5_out), .in1(3'b000), .out(multiplexer_6_out), .sel(xor_1_out));
  Multiplexer #(.select(2), .width(3), .enable("false")) multiplexer_7 (
    .in0(multiplexer_6_out), .in1(subtractor_2_out), .in2(subtractor_1_out), .in3(subtractor_1_out),
    .out(STEPS), .sel({Yf_Yi_2, Xf_Xi_2}));

  // Notes on the sheet:
  //   S: pull=down
  //   SELECT PIECE
  //   NEW POSITON INPUT
  //   NUMBER OF STEPS CALCULATOR
  //   NUMBER OF STERPS TO MOVE
endmodule

module COUNTER (
  input  CLK,
  input  BUTTON,
  input  [2:0] STEPS_TO_TAKE,
  output [3:0] STATE
);

  wire and_1_out, and_2_out, and_3_out, and_4_out, and_5_out, and_6_out, and_7_out, and_8_out, and_9_out,
       D0_qn, not_1_out, not_2_out, not_3_out, or_1_out, or_2_out, or_3_out, xnor_1_out;

  not not_1 (not_1_out, STATE[0]);
  not not_2 (not_2_out, STATE[1]);
  not not_3 (not_3_out, STATE[2]);
  and and_1 (and_1_out, not_3_out, not_2_out, not_1_out);
  and and_2 (and_2_out, 1'b1, BUTTON);
  and and_3 (and_3_out, or_1_out, STATE[2]);
  D_Flip_Flop D3 (.clk(CLK), .D(and_1_out), .Q(STATE[3]), .reset(and_2_out));  // open: Qn, preset, en
  D_Flip_Flop D2 (.clk(CLK), .D(and_3_out), .Q(STATE[2]), .preset(and_4_out));  // open: Qn, en, reset
  and and_4 (and_4_out, BUTTON, STEPS_TO_TAKE[2]);
  or or_1 (or_1_out, STATE[0], STATE[1]);
  and and_5 (and_5_out, or_3_out, and_7_out);
  D_Flip_Flop D1 (.clk(CLK), .D(and_5_out), .Q(STATE[1]), .preset(and_6_out));  // open: Qn, en, reset
  and and_6 (and_6_out, BUTTON, STEPS_TO_TAKE[1]);
  and and_7 (and_7_out, or_2_out, xnor_1_out);
  xnor xnor_1 (xnor_1_out, STATE[0], STATE[1]);
  or or_2 (or_2_out, STATE[2], STATE[0]);
  D_Flip_Flop D0 (.clk(CLK), .D(and_9_out), .Q(STATE[0]), .Qn(D0_qn), .preset(and_8_out));  // open: en, reset
  or or_3 (or_3_out, STATE[2], STATE[1]);
  and and_8 (and_8_out, BUTTON, STEPS_TO_TAKE[0]);
  and and_9 (and_9_out, or_3_out, D0_qn);

  // Notes on the sheet:
  //   COUNTER CIRCUIT
endmodule

module DIRECTION_CHECKER (
  input  in_1,
  input  piece_value,
  input  Xf_Xi,
  input  Xf_Xi_2,
  input  Yf_Yi,
  input  Yf_Yi_2,
  output [3:0] Direction
);

  wire or_1_out;
  wire [3:0] multiplexer_1_out, multiplexer_2_out, multiplexer_3_out, multiplexer_4_out;

  or or_1 (or_1_out, in_1, piece_value);
  Multiplexer #(.width(4), .enable("false")) multiplexer_1 (
    .in0(4'b0100), .in1(4'b1001), .out(multiplexer_1_out), .sel(or_1_out));
  Multiplexer #(.width(4), .enable("false")) multiplexer_2 (
    .in0(4'b0101), .in1(4'b1001), .out(multiplexer_2_out), .sel(or_1_out));
  Multiplexer #(.width(4), .enable("false")) multiplexer_3 (
    .in0(4'b0111), .in1(4'b1001), .out(multiplexer_3_out), .sel(or_1_out));
  Multiplexer #(.width(4), .enable("false")) multiplexer_4 (
    .in0(4'b0110), .in1(4'b1001), .out(multiplexer_4_out), .sel(or_1_out));
  Multiplexer #(.select(4), .width(4), .enable("false")) multiplexer_5 (
    .in0(multiplexer_1_out), .in1(4'b0001), .in2(multiplexer_2_out), .in4(4'b0000), .in5(4'b1001),
    .in6(4'b0010), .in8(multiplexer_3_out), .in9(4'b0011), .in10(multiplexer_4_out), .out(Direction),
    .sel({Xf_Xi, Xf_Xi_2, Yf_Yi, Yf_Yi_2}));  // open: in3, in7, in11, in12, in13, in14, in15

  // Notes on the sheet:
  //   DIRECTION CHECKER CIRCUIT
endmodule

module POSITION_SAVER (
  input  [2:0] Xf,
  input  [2:0] Yf,
  input  [1:0] S,
  input  Register_Clock_Control,
  input  [2:0] Set_X,
  input  [2:0] Set_Y,
  input  Set_Default,
  input  Set,
  output [2:0] Xi,
  output [2:0] Yi
);

  wire decoder_1_out0, decoder_1_out1, decoder_1_out2, undriven, xor_1_out;
  wire [2:0] multiplexer_1_out, multiplexer_2_out, multiplexer_3_out, x_2_q, x_q, y_2_q, y_q;
  wire [5:0] y_3_q;

  Decoder #(.select(2), .enable("false")) decoder_1 (
    .out0(decoder_1_out0), .out1(decoder_1_out1), .out2(decoder_1_out2), .sel(S));  // open: out3
  Multiplexer #(.select(2), .width(3), .enable("false")) multiplexer_1 (
    .in0(Xf), .in1(Set_X), .in2(3'b000), .out(multiplexer_1_out), .sel({Set_Default, Set}));  // open: in3
  Multiplexer #(.select(2), .width(3), .enable("false")) multiplexer_2 (
    .in0(3'b100), .in1(3'b000), .in2(3'b111), .out(multiplexer_2_out), .sel(S));  // open: in3
  Multiplexer #(.select(2), .width(3), .enable("false")) multiplexer_3 (
    .in0(Yf), .in1(Set_Y), .in2(multiplexer_2_out), .out(multiplexer_3_out), .sel({Set_Default, Set}));  // open: in3
  Register #(.width(3)) y (.D(multiplexer_1_out), .en(decoder_1_out0), .Q(y_q), .clk(xor_1_out));  // open: clr
  Register #(.width(3)) x (.D(multiplexer_3_out), .en(decoder_1_out0), .Q(x_q), .clk(xor_1_out));  // open: clr
  Register #(.width(3)) y_2 (.D(multiplexer_1_out), .en(decoder_1_out1), .Q(y_2_q), .clk(xor_1_out), .clr(undriven));
  Multiplexer #(.select(2), .width(6), .enable("false")) multiplexer_4 (
    .in0({x_q, y_q}), .in1({x_2_q, y_2_q}), .in2(y_3_q), .out({Yi, Xi}), .sel(S));  // open: in3
  Register #(.width(3)) x_2 (.D(multiplexer_3_out), .en(decoder_1_out1), .Q(x_2_q), .clk(xor_1_out));  // open: clr
  Register #(.width(3)) x_3 (.D(multiplexer_3_out), .en(decoder_1_out2), .Q(y_3_q[5:3]), .clk(xor_1_out));  // open: clr
  Register #(.width(3)) y_3 (.D(multiplexer_1_out), .en(decoder_1_out2), .Q(y_3_q[2:0]), .clk(xor_1_out));  // open: clr
  ExactlyOne xor_1 (.out(xor_1_out), .in0(Set_Default), .in1(Set), .in2(Register_Clock_Control));

  // Notes on the sheet:
  //   QUEEN I'
  //   POSITION SAVER CIRCUIT 
  //   ROOK 1 I
  //   ROOK 2 I
endmodule

module MAIN_CIRCUIT_CHIP (
  input  [1:0] S_PIECE_CODE,
  input  [2:0] Xf_FINAL_X_COORDINATE,
  input  [2:0] Yf_FINAL_Y_COORDINATE,
  input  [2:0] Set_X,
  input  [2:0] Set_Y,
  output [2:0] STEPS_LEFT_TO_TAKE,
  output [3:0] DIRECTION_TO_MOVE
);

  wire and_1_out, comparator_1_eq, comparator_1_gt, comparator_1_lt, comparator_2_eq, comparator_2_gt,
       comparator_2_lt, MAIN_CLOCK_out, Move_out, multiplexer_1_out, nor_1_out, nor_2_out, nor_3_out,
       not_1_out, Set_Default_out, Set_out;
  wire [1:0] or_1_out;
  wire [2:0] Position_Register_xi, Position_Register_yi, steps_calculator_1_steps;
  wire [3:0] direction_checker_1_direction;

  Clock MAIN_CLOCK (.out(MAIN_CLOCK_out));
  Button Move (.out(Move_out));
  Button Set (.out(Set_out));
  Button Set_Default (.out(Set_Default_out));
  Comparator #(.width(3), .mode("unsigned")) comparator_1 (
    .a(Xf_FINAL_X_COORDINATE), .b(Position_Register_xi), .gt(comparator_1_gt), .eq(comparator_1_eq),
    .lt(comparator_1_lt));
  Comparator #(.width(3), .mode("unsigned")) comparator_2 (
    .a(Yf_FINAL_Y_COORDINATE), .b(Position_Register_yi), .gt(comparator_2_gt), .eq(comparator_2_eq),
    .lt(comparator_2_lt));
  Hex_Digit_Display hex_digit_display_1 (.value({1'b0, Position_Register_xi}));  // open: dp
  Hex_Digit_Display hex_digit_display_2 (.value({1'b0, Position_Register_yi}));  // open: dp
  POSITION_SAVER Position_Register (
    .Yf(Yf_FINAL_Y_COORDINATE), .S(S_PIECE_CODE), .Xi(Position_Register_xi), .Yi(Position_Register_yi),
    .Set_Default(Set_Default_out), .Xf(Xf_FINAL_X_COORDINATE), .Set_X(Set_X),
    .Register_Clock_Control(multiplexer_1_out), .Set_Y(Set_Y), .Set(Set_out));
  DIRECTION_CHECKER direction_checker_1 (
    .in_1(S_PIECE_CODE[0]), .piece_value(S_PIECE_CODE[1]), .Xf_Xi(comparator_1_gt),
    .Xf_Xi_2(comparator_1_eq), .Yf_Yi(comparator_2_gt), .Yf_Yi_2(comparator_2_eq),
    .Direction(direction_checker_1_direction));
  Multiplexer #(.enable("false")) multiplexer_1 (
    .in0(or_1_out[1]), .in1(1'b1), .out(multiplexer_1_out), .sel(nor_1_out));
  nor nor_1 (nor_1_out, steps_calculator_1_steps[0], steps_calculator_1_steps[1], steps_calculator_1_steps[2]);
  STEPS_CALCULATOR steps_calculator_1 (
    .S(S_PIECE_CODE), .Xf(Xf_FINAL_X_COORDINATE), .Yf(Yf_FINAL_Y_COORDINATE), .Xf_Xi(comparator_1_gt),
    .Xf_Xi_2(comparator_1_eq), .Xf_Xi_3(comparator_1_lt), .Yf_Yi(comparator_2_gt), .Yf_Yi_2(comparator_2_eq),
    .Yf_Yi_3(comparator_2_lt), .Xi(Position_Register_xi), .Yi(Position_Register_yi),
    .STEPS(steps_calculator_1_steps));
  COUNTER Counter (
    .CLK(MAIN_CLOCK_out), .BUTTON(Move_out), .STEPS_TO_TAKE(steps_calculator_1_steps),
    .STATE({or_1_out[1], STEPS_LEFT_TO_TAKE}));
  not not_1 (not_1_out, or_1_out[1]);
  and and_1 (and_1_out, Move_out, nor_1_out);
  nor nor_2 (nor_2_out, STEPS_LEFT_TO_TAKE[0], STEPS_LEFT_TO_TAKE[1], STEPS_LEFT_TO_TAKE[2]);
  LED led_1 (.in(not_1_out));
  Multiplexer #(.select(2), .width(4), .enable("false")) multiplexer_2 (
    .in0(direction_checker_1_direction), .in1(4'b1001), .in2(4'b1001), .in3(4'b1001),
    .out(DIRECTION_TO_MOVE), .sel(or_1_out));
  or or_1 (or_1_out[0], nor_2_out, nor_3_out);
  nor nor_3 (nor_3_out, nor_2_out, MAIN_CLOCK_out);
  LED LED_BLINKS_WHEN_WRONG_INPUT__IS_GIVEN (.in(and_1_out));
  Hex_Digit_Display hex_digit_display_3 (.value(DIRECTION_TO_MOVE));  // open: dp

  // Notes on the sheet:
  //   CHESS BOARD AUTOMATER CHIP FOR QUEEN AND 2 ROOKS 
  //   COORDINATE COMPARATOR
  //   CURRENT POSITION (X,Y)
  //   DIRECTION OUTPUT
  //   LED SHOWING IF MOVEMENT ONGOING
endmodule
